# Fritzing sketch schematics (saved by Fritzing 0.9.3b)
breadboards: 1

parts:
  Part1 = Arduino Uno (Rev3)
  Yellow_LED = LED - 5mm [color="Yellow (592nm)" package="5 mm [THT]"]
  R2 = Resistor [tolerance=±5% resistance=220 package=THT]
  R1 = Resistor [tolerance=±5% resistance=220 package=THT]
  Red_LED = LED - 5mm [color="Red (633nm)" package="5 mm [THT]"]

nets:
  N1: Part1.D5_PWM, R1.Pin_1
  N2: Part1.D6_PWM, R2.Pin_0
  N3: Part1.GND, Yellow_LED.cathode, Red_LED.cathode
  N4: Yellow_LED.anode, R2.Pin_1
  N5: R1.Pin_0, Red_LED.anode
