# Fritzing sketch schematics (saved by Fritzing 0.9.3b)
breadboards: 1

parts:
  Part_1 = Arduino Uno (Rev3)
  R1 = Resistor [tolerance=±5% resistance=220 package=THT]
  Red_LED = LED - 5mm [color="Red (633nm)" package="5 mm [THT]"]
  Potentiometer = Rotary Potentiometer (Small) [maximum_resistance=10kΩ package=THT]

nets:
  N1: Part_1.A0, Potentiometer.wiper
  N2: Part_1.GND, Red_LED.cathode, Potentiometer.leg1
  N3: Part_1.D5_PWM, R1.Pin_1
  N4: Part_1.5V, Potentiometer.leg2
  N5: R1.Pin_0, Red_LED.anode
